# Fritzing sketch perler_tool (saved by Fritzing 0.9.3b)
breadboards: 1
perfboards: 1

parts:
  Raspberry_Pi_1 = Raspberry Pi 3 [part_number=RPI-3-V1.2]
  CameraLight = LEDs [package=led10mm]
  R4 = Resistor [tolerance=±5% resistance=220 package="2010 [SMD]"]
  J1 = Basic Servo
  M1 = DC Motor
  Mosfet_driver_module1 = IFR520 MOS module [package=THT]
  External_5v = 2.1mm Barrel Jack with Terminal Block
  External_5v1 = 2.1mm Barrel Jack with Terminal Block  # not connected
  J2 = Camdenboss CTB0158-2 [part_number=CTB0158-2 package=THT]  # not connected
  J3 = Basic Servo
  CameraLight1 = LEDs [package=led10mm]  # not connected
  J4 = Camdenboss CTB0158-2 [part_number=CTB0158-2 package=THT]
  Raspberry_Pi_2 = Raspberry Pi 3 [part_number=RPI-3-V1.2]
  J5 = Camdenboss CTB0158-2 [part_number=CTB0158-2 package=THT]
  J6 = Camdenboss CTB0158-2 [part_number=CTB0158-2 package=THT]
  Mosfet_driver_module2 = IFR520 MOS module [package=THT]  # not connected
  J7 = Camdenboss CTB0158-2 [part_number=CTB0158-2 package=THT]  # not connected
  J8 = Camdenboss CTB0158-2 [part_number=CTB0158-2 package=THT]  # not connected
  J9 = Camdenboss CTB0158-2 [part_number=CTB0158-2 package=THT]  # not connected
  J10 = Camdenboss CTB0158-2 [part_number=CTB0158-2 package=THT]  # not connected

nets:
  N1: Raspberry_Pi_1.GPIO24, Mosfet_driver_module1.pin1
  N2: Raspberry_Pi_1.GPIO23, J1.pulse
  N3: Raspberry_Pi_1.GND, Mosfet_driver_module1.pin3
  N4: Raspberry_Pi_1.5V, Mosfet_driver_module1.pin2
  N5: CameraLight.C, J1.gnd, Mosfet_driver_module1.pin7, External_5v.NEG
  N6: CameraLight.A, R4.Pin_0
  N7: R4.Pin_1, J1.vcc, Mosfet_driver_module1.pin6, External_5v.POS
  N8: M1.pin_1, Mosfet_driver_module1.pin4
  N9: M1.pin_2, Mosfet_driver_module1.pin5
  N10: J3.gnd, J5.terminal_2
  N11: J3.vcc, J5.terminal_1
  N12: J3.pulse, J6.terminal_2
  N13: J4.terminal_1, Raspberry_Pi_2.GND
  N14: J4.terminal_2, Raspberry_Pi_2.5V

custom parts:
  IFR520 MOS module: Breakout board for the IFR520 MOSFET transistor. The module is designed to switch heavy DC loads from a single digital pin of your microcontroller. Its main purpose is to provide a low cost way to drive a DC motor for robotics applications, but the module can be used to control most high current DC loads. Screw terminals are provided to interface to your load and external power source. An LED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
